# Fritzing sketch Schematic_Hoermann_GTO90 (saved by Fritzing 0.9.3b)
breadboards: 1

parts:
  WeMos_D1_Mini1 = WeMos D1 Mini
  R1 = Resistor [tolerance=±5% resistance=2.0k package="0805 [SMD]"]
  Q1 = NPN-Transistor [package="TO92 [THT]"]
  R2 = Resistor [tolerance=±5% resistance=200k package="0805 [SMD]"]
  R3 = Resistor [tolerance=±5% resistance=27k package="0805 [SMD]"]
  R4 = Resistor [tolerance=±5% resistance=200k package="0805 [SMD]"]
  R5 = Resistor [tolerance=±5% resistance=27k package="0805 [SMD]"]
  R6 = Resistor [tolerance=±5% resistance=200k package="0805 [SMD]"]
  R7 = Resistor [tolerance=±5% resistance=27k package="0805 [SMD]"]
  R8 = Resistor [tolerance=±5% resistance=200k package="0805 [SMD]"]
  R9 = Resistor [tolerance=±5% resistance=27k package="0805 [SMD]"]
  M1 = fc-51 [package=THT]
  Q2 = NPN-Transistor [package="TO92 [THT]"]
  R10 = Resistor [tolerance=±5% resistance=2.0k package="0805 [SMD]"]
  HLK-PM1 = HLK-PM12 [part_number=HLK-PM12]
  End_UP_-_gelb = Header 1 [package=pad-1.5x4.5]
  MovDnOrEnd_-_orange = Header 1 [package=pad-1.5x4.5]
  Taster_-_pink = Header 1 [package=pad-1.5x4.5]
  Taster_2_-_N/A = Header 1 [package=pad-1.5x4.5]
  End_DN_-_grün = Header 1 [package=pad-1.5x4.5]
  MovUpOrEnd_-_weiß = Header 1 [package=pad-1.5x4.5]
  Rot_-_26V = Header 1 [package=pad-1.5x4.5]
  Schwarz_-_GND = Header 1 [package=pad-1.5x4.5]

nets:
  N1: WeMos_D1_Mini1.3V3, M1.pin3, HLK-PM1.+Vo
  N2: WeMos_D1_Mini1.D0, R2.Pin_1, R3.Pin_0
  N3: WeMos_D1_Mini1.D1, R8.Pin_1, R9.Pin_0
  N4: WeMos_D1_Mini1.D2, R4.Pin_1, R5.Pin_0
  N5: WeMos_D1_Mini1.D5, R6.Pin_1, R7.Pin_0
  N6: WeMos_D1_Mini1.D6, M1.pin1
  N7: WeMos_D1_Mini1.D7, R10.Pin_1
  N8: WeMos_D1_Mini1.D8, R1.Pin_1
  N9: WeMos_D1_Mini1.G, Q1.E, R3.Pin_1, R5.Pin_1, R7.Pin_1, R9.Pin_1, M1.pin2, Q2.E, HLK-PM1.-Vo
  N10: R1.Pin_0, Q1.B
  N11: Q1.C, Taster_-_pink.1
  N12: R2.Pin_0, End_UP_-_gelb.1
  N13: R4.Pin_0, End_DN_-_grün.1
  N14: R6.Pin_0, MovDnOrEnd_-_orange.1
  N15: R8.Pin_0, MovUpOrEnd_-_weiß.1
  N16: Q2.B, R10.Pin_0
  N17: Q2.C, Taster_2_-_N/A.1
  N18: HLK-PM1.AC_1, Rot_-_26V.1
  N19: HLK-PM1.AC_2, Schwarz_-_GND.1
